# Fritzing sketch montage (saved by Fritzing 0.9.3b)
breadboards: 1

parts:
  R1 = Resistor [tolerance=±5% resistance=10k package=THT]
  Composant1 = Arduino Uno (Rev3)
  R2 = Temperature Sensor (Thermistor) [thermistor_type=NTC package=THT]
  R3 = Resistor [tolerance=±5% resistance=10k package=THT]
  R4 = Resistor [tolerance=±5% resistance=1.5k package=THT]
  Q1 = Basic FET N-Channel [package="DPak [SMD]"]
  DHT2 = DHT22 Humidity and Temperature Sensor
  USBTTL1 = adafruit
  J1 = Peltier Element

nets:
  N1: R1.Pin_0, Composant1.A0, R2.pin_1
  5V: R1.Pin_1, Composant1.5V, R3.Pin_0, DHT2.VDD
  N2: Composant1.A5/SCL, R4.Pin_0, Q1.Gate
  N3: Composant1.D2, R3.Pin_1, DHT2.DATA
  GND: Composant1.GND, R2.pin_0, DHT2.GND
  N4: R4.Pin_1, USBTTL1.connector3, J1.pin2
  N5: Q1.drain, J1.pin1
  N6: Q1.source, USBTTL1.connector4
